// Logisim project lab4.circ as structural Verilog: 12 circuits, main circuit main
module main (
);

  wire alu_control_1_alu_src, and_1_out, clock_1_out, comparator_1_eq, control_1_branch, control_1_memread,
       control_1_memtoreg, control_1_memwrite, control_1_regwrite;
  wire [3:0] alu_control_1_alu_ctrl0;
  wire [7:0] register_1_q_2;
  wire [23:0] register_1_q;
  wire [31:0] adder_1_out, adder_2_out, datamemory_1_readdata, immgen_1_imm32,
       instructionmemory16mb_1_instruction, multiplexer_1_out, multiplexer_2_out, multiplexer_3_out,
       register_file_1_rdata1, register_file_1_rdata2, thirty_two_alu_1_result;

  Register #(.width(32)) register_1 (
    .D(multiplexer_2_out), .en(1'b1), .clk(clock_1_out), .Q({register_1_q_2, register_1_q}));  // open: clr
  Clock clock_1 (.out(clock_1_out));
  Adder #(.width(32)) adder_1 (.a({register_1_q_2, register_1_q}), .b(32'h4), .out(adder_1_out));  // open: cin, cout
  InstructionMemory16MB instructionmemory16mb_1 (
    .Address(register_1_q), .ClockIn(clock_1_out), .Instruction(instructionmemory16mb_1_instruction));
  ImmGen immgen_1 (.Instruction(instructionmemory16mb_1_instruction), .IMM32(immgen_1_imm32));
  Control control_1 (
    .I6(instructionmemory16mb_1_instruction[6]), .I5(instructionmemory16mb_1_instruction[5]),
    .I4(instructionmemory16mb_1_instruction[4]), .I3(instructionmemory16mb_1_instruction[3]),
    .I2(instructionmemory16mb_1_instruction[2]), .I1(instructionmemory16mb_1_instruction[1]),
    .I0(instructionmemory16mb_1_instruction[0]), .MemtoReg(control_1_memtoreg),
    .RegWrite(control_1_regwrite), .MemRead(control_1_memread), .MemWrite(control_1_memwrite),
    .Branch(control_1_branch));
  register_file register_file_1 (
    .RReg1(instructionmemory16mb_1_instruction[19:15]), .RReg2(instructionmemory16mb_1_instruction[24:20]),
    .WData(multiplexer_3_out), .Clock_in(clock_1_out), .Write(control_1_regwrite),
    .WReg(instructionmemory16mb_1_instruction[11:7]), .RData1(register_file_1_rdata1),
    .RData2(register_file_1_rdata2));
  ALU_Control alu_control_1 (
    .I30(instructionmemory16mb_1_instruction[30]), .I14(instructionmemory16mb_1_instruction[14]),
    .I13(instructionmemory16mb_1_instruction[13]), .I12(instructionmemory16mb_1_instruction[12]),
    .I6(instructionmemory16mb_1_instruction[6]), .I5(instructionmemory16mb_1_instruction[5]),
    .I4(instructionmemory16mb_1_instruction[4]), .ALU_Ctrl3(alu_control_1_alu_ctrl0[3]),
    .ALU_Ctrl2(alu_control_1_alu_ctrl0[2]), .ALU_Ctrl1(alu_control_1_alu_ctrl0[1]),
    .ALU_Ctrl0(alu_control_1_alu_ctrl0[0]), .ALU_Src(alu_control_1_alu_src));
  Multiplexer #(.enable("false"), .width(32)) multiplexer_1 (
    .in0(register_file_1_rdata2), .in1(immgen_1_imm32), .out(multiplexer_1_out), .sel(alu_control_1_alu_src));
  Comparator #(.width(32)) comparator_1 (
    .a(register_file_1_rdata1), .b(register_file_1_rdata2), .eq(comparator_1_eq));  // open: gt, lt
  thirty_two_ALU thirty_two_alu_1 (
    .ALU_Ctrl(alu_control_1_alu_ctrl0), .A(register_file_1_rdata1), .B(multiplexer_1_out),
    .Result(thirty_two_alu_1_result));  // open: C_out
  Adder #(.width(32)) adder_2 (
    .a({register_1_q_2, register_1_q}), .b(immgen_1_imm32), .out(adder_2_out));  // open: cin, cout
  and and_1 (and_1_out, control_1_branch, comparator_1_eq);
  Multiplexer #(.enable("false"), .width(32)) multiplexer_2 (
    .in0(adder_1_out), .in1(adder_2_out), .out(multiplexer_2_out), .sel(and_1_out));
  DataMemory datamemory_1 (
    .Address(thirty_two_alu_1_result[25:0]), .MemWrite(control_1_memwrite), .MemRead(control_1_memread),
    .ClockIn(clock_1_out), .WriteData(register_file_1_rdata2), .ReadData(datamemory_1_readdata));
  Multiplexer #(.enable("false"), .width(32)) multiplexer_3 (
    .in0(thirty_two_alu_1_result), .in1(datamemory_1_readdata), .out(multiplexer_3_out),
    .sel(control_1_memtoreg));
endmodule

module ImmGen (
  input  [31:0] Instruction,
  output [31:0] IMM32
);

  assign IMM32[31:12] = {{19{Instruction[31]}}, Instruction[31]};  // Bit_Extender bit_extender_1
  Multiplexer #(.enable("false"), .select(2)) multiplexer_1 (
    .in0(Instruction[20]), .in1(Instruction[7]), .in3(1'b0), .out(IMM32[0]), .sel(Instruction[6:5]));  // open: in2
  Multiplexer #(.enable("false"), .width(4)) multiplexer_2 (
    .in0(Instruction[24:21]), .in1(Instruction[11:8]), .out(IMM32[4:1]), .sel(Instruction[5]));
  Multiplexer #(.enable("false")) multiplexer_3 (
    .in0(Instruction[31]), .in1(Instruction[7]), .out(IMM32[11]), .sel(Instruction[6]));

  assign IMM32[10:5] = Instruction[30:25];

  // Other names for the same wires on the sheet: I30_25[5:0] = Instruction[30:25]; I5 = Instruction[5];
  //   I6_5[1:0] = Instruction[6:5]; I6 = Instruction[6]; I7 = Instruction[7]; I11_8[3:0] = Instruction[11:8];
  //   I_20 = Instruction[20]; I24_21[3:0] = Instruction[24:21]; I31 = Instruction[31]
endmodule

module InstructionMemory16MB (
  input  [23:0] Address,
  input  ClockIn,
  output [31:0] Instruction
);

  wire not_1_out;

  not not_1 (not_1_out, ClockIn);
  RAM #(.addrWidth(22), .asyncread("true"), .dataWidth(32)) ram_1 (
    .addr(Address[23:2]), .we(1'b0), .oe(not_1_out), .dout(Instruction));  // open: clk, din
endmodule

module Control (
  input  I6,
  input  I5,
  input  I4,
  input  I3,
  input  I2,
  input  I1,
  input  I0,
  output MemtoReg,
  output RegWrite,
  output MemRead,
  output MemWrite,
  output Branch
);

  wire not_1_out, not_2_out, not_3_out;

  not not_1 (not_1_out, I6);
  not not_2 (not_2_out, I5);
  not not_3 (not_3_out, I4);
  and and_1 (MemtoReg, not_2_out, not_3_out);
  or or_1 (RegWrite, not_2_out, I4);
  and and_2 (MemRead, not_2_out, not_3_out);
  and and_3 (MemWrite, not_1_out, I5, not_3_out);

  assign Branch = I6;
endmodule

module DataMemory (
  input  [25:0] Address,
  input  MemWrite,
  input  MemRead,
  input  ClockIn,
  input  [31:0] WriteData,
  output [31:0] ReadData
);

  RAM #(.addrWidth(24), .asyncread("true"), .dataWidth(32)) ram_1 (
    .addr(Address[25:2]), .we(MemWrite), .oe(MemRead), .clk(ClockIn), .din(WriteData), .dout(ReadData));
endmodule

module register_file (
  input  [4:0] RReg1,
  input  [4:0] RReg2,
  input  [31:0] WData,
  input  Clock_in,
  input  Write,
  input  [4:0] WReg,
  output [31:0] RData1,
  output [31:0] RData2
);

  wire W3_0, W7_4, W11_8, W15_12, W19_16, W23_20, W27_24, W31_28;
  wire [31:0] register_file_4bit_1_rdata1, register_file_4bit_1_rdata2, register_file_4bit_2_rdata1,
       register_file_4bit_2_rdata2, register_file_4bit_3_rdata1, register_file_4bit_3_rdata2,
       register_file_4bit_4_rdata1, register_file_4bit_4_rdata2, register_file_4bit_5_rdata1,
       register_file_4bit_5_rdata2, register_file_4bit_6_rdata1, register_file_4bit_6_rdata2,
       register_file_4bit_7_rdata1, register_file_4bit_7_rdata2, register_file_4bit_8_rdata1,
       register_file_4bit_8_rdata2;

  Demultiplexer #(.enable("false"), .select(3)) demultiplexer_1 (
    .out0(W3_0), .out1(W7_4), .out2(W11_8), .out3(W15_12), .out4(W19_16), .out5(W23_20), .out6(W27_24),
    .out7(W31_28), .in(Write), .sel(WReg[4:2]));
  register_file_4bit register_file_4bit_1 (
    .Reg1(RReg1[1:0]), .Reg2(RReg2[1:0]), .WData(WData), .Clock_in(Clock_in), .Write(W3_0), .WReg(WReg[1:0]),
    .RData1(register_file_4bit_1_rdata1), .RData2(register_file_4bit_1_rdata2));
  register_file_4bit register_file_4bit_2 (
    .Reg1(RReg1[1:0]), .Reg2(RReg2[1:0]), .WData(WData), .Clock_in(Clock_in), .Write(W7_4), .WReg(WReg[1:0]),
    .RData1(register_file_4bit_2_rdata1), .RData2(register_file_4bit_2_rdata2));
  register_file_4bit register_file_4bit_3 (
    .Reg1(RReg1[1:0]), .Reg2(RReg2[1:0]), .WData(WData), .Clock_in(Clock_in), .Write(W11_8),
    .WReg(WReg[1:0]), .RData1(register_file_4bit_3_rdata1), .RData2(register_file_4bit_3_rdata2));
  register_file_4bit register_file_4bit_4 (
    .Reg1(RReg1[1:0]), .Reg2(RReg2[1:0]), .WData(WData), .Clock_in(Clock_in), .Write(W15_12),
    .WReg(WReg[1:0]), .RData1(register_file_4bit_4_rdata1), .RData2(register_file_4bit_4_rdata2));
  register_file_4bit register_file_4bit_5 (
    .Reg1(RReg1[1:0]), .Reg2(RReg2[1:0]), .WData(WData), .Clock_in(Clock_in), .Write(W19_16),
    .WReg(WReg[1:0]), .RData1(register_file_4bit_5_rdata1), .RData2(register_file_4bit_5_rdata2));
  register_file_4bit register_file_4bit_6 (
    .Reg1(RReg1[1:0]), .Reg2(RReg2[1:0]), .WData(WData), .Clock_in(Clock_in), .Write(W23_20),
    .WReg(WReg[1:0]), .RData1(register_file_4bit_6_rdata1), .RData2(register_file_4bit_6_rdata2));
  register_file_4bit register_file_4bit_7 (
    .Reg1(RReg1[1:0]), .Reg2(RReg2[1:0]), .WData(WData), .Clock_in(Clock_in), .Write(W27_24),
    .WReg(WReg[1:0]), .RData1(register_file_4bit_7_rdata1), .RData2(register_file_4bit_7_rdata2));
  register_file_4bit register_file_4bit_8 (
    .Reg1(RReg1[1:0]), .Reg2(RReg2[1:0]), .WData(WData), .Clock_in(Clock_in), .Write(W31_28),
    .WReg(WReg[1:0]), .RData1(register_file_4bit_8_rdata1), .RData2(register_file_4bit_8_rdata2));
  Multiplexer #(.enable("false"), .select(3), .width(32)) multiplexer_1 (
    .in0(register_file_4bit_1_rdata1), .in1(register_file_4bit_2_rdata1), .in2(register_file_4bit_3_rdata1),
    .in3(register_file_4bit_4_rdata1), .in4(register_file_4bit_5_rdata1), .in5(register_file_4bit_6_rdata1),
    .in6(register_file_4bit_7_rdata1), .in7(register_file_4bit_8_rdata1), .out(RData1), .sel(RReg1[4:2]));
  Multiplexer #(.enable("false"), .select(3), .width(32)) multiplexer_2 (
    .in0(register_file_4bit_1_rdata2), .in1(register_file_4bit_2_rdata2), .in2(register_file_4bit_3_rdata2),
    .in3(register_file_4bit_4_rdata2), .in4(register_file_4bit_5_rdata2), .in5(register_file_4bit_6_rdata2),
    .in6(register_file_4bit_7_rdata2), .in7(register_file_4bit_8_rdata2), .out(RData2), .sel(RReg2[4:2]));
endmodule

module register_file_4bit (
  input  [1:0] Reg1,
  input  [1:0] Reg2,
  input  [31:0] WData,
  input  Clock_in,
  input  Write,
  input  [1:0] WReg,
  output [31:0] RData1,
  output [31:0] RData2
);

  wire demultiplexer_1_out0, demultiplexer_1_out1, demultiplexer_1_out2, demultiplexer_1_out3;
  wire [31:0] register_1_q, register_2_q, register_3_q, register_4_q;

  Demultiplexer #(.enable("false"), .select(2)) demultiplexer_1 (
    .out0(demultiplexer_1_out0), .out1(demultiplexer_1_out1), .out2(demultiplexer_1_out2),
    .out3(demultiplexer_1_out3), .in(Write), .sel(WReg));
  Register #(.width(32)) register_1 (
    .D(WData), .en(demultiplexer_1_out0), .clk(Clock_in), .Q(register_1_q), .clr(Write));
  Register #(.width(32)) register_2 (
    .D(WData), .en(demultiplexer_1_out1), .clk(Clock_in), .Q(register_2_q));  // open: clr
  Register #(.width(32)) register_3 (
    .D(WData), .en(demultiplexer_1_out2), .clk(Clock_in), .Q(register_3_q));  // open: clr
  Register #(.width(32)) register_4 (
    .D(WData), .en(demultiplexer_1_out3), .clk(Clock_in), .Q(register_4_q));  // open: clr
  Multiplexer #(.enable("false"), .select(2), .width(32)) multiplexer_1 (
    .in0(register_1_q), .in1(register_2_q), .in2(register_3_q), .in3(register_4_q), .out(RData1), .sel(Reg1));
  Multiplexer #(.enable("false"), .select(2), .width(32)) multiplexer_2 (
    .in0(register_1_q), .in1(register_2_q), .in2(register_3_q), .in3(register_4_q), .out(RData2), .sel(Reg2));
endmodule

module one_bit_ALU (
  input  [3:0] ALU_Ctrl,
  input  A,
  input  B,
  input  C_in,
  output R,
  output C_out
);

  wire and_1_out, multiplexer_1_out, not_1_out, one_bit_adder_1_s, or_1_out, xor_1_out;

  not not_1 (not_1_out, B);
  Multiplexer #(.enable("false")) multiplexer_1 (.in0(B), .in1(not_1_out), .out(multiplexer_1_out), .sel(ALU_Ctrl[2]));
  and and_1 (and_1_out, A, multiplexer_1_out);
  or or_1 (or_1_out, A, multiplexer_1_out);
  xor xor_1 (xor_1_out, A, multiplexer_1_out);
  one_bit_adder one_bit_adder_1 (.A(A), .B(multiplexer_1_out), .C_in(C_in), .S(one_bit_adder_1_s), .C_out(C_out));
  Multiplexer #(.enable("false"), .select(2)) multiplexer_2 (
    .in0(and_1_out), .in1(or_1_out), .in2(xor_1_out), .in3(one_bit_adder_1_s), .out(R), .sel(ALU_Ctrl[1:0]));
endmodule

module four_bit_ALU (
  input  [3:0] ALU_Ctrl,
  input  [3:0] A,
  input  [3:0] B,
  input  C_in,
  output [3:0] R,
  output C_out
);

  wire one_bit_alu_1_c_out, one_bit_alu_2_c_out, one_bit_alu_3_c_out;

  one_bit_ALU one_bit_alu_1 (
    .ALU_Ctrl(ALU_Ctrl), .A(A[0]), .B(B[0]), .C_in(C_in), .R(R[0]), .C_out(one_bit_alu_1_c_out));
  one_bit_ALU one_bit_alu_2 (
    .ALU_Ctrl(ALU_Ctrl), .A(A[1]), .B(B[1]), .C_in(one_bit_alu_1_c_out), .R(R[1]), .C_out(one_bit_alu_2_c_out));
  one_bit_ALU one_bit_alu_3 (
    .ALU_Ctrl(ALU_Ctrl), .A(A[2]), .B(B[2]), .C_in(one_bit_alu_2_c_out), .R(R[2]), .C_out(one_bit_alu_3_c_out));
  one_bit_ALU one_bit_alu_4 (
    .ALU_Ctrl(ALU_Ctrl), .A(A[3]), .B(B[3]), .C_in(one_bit_alu_3_c_out), .R(R[3]), .C_out(C_out));
endmodule

module thirty_two_ALU (
  input  [3:0] ALU_Ctrl,
  input  [31:0] A,
  input  [31:0] B,
  output [31:0] Result,
  output C_out
);

  wire four_bit_alu_1_c_out, four_bit_alu_2_c_out, four_bit_alu_3_c_out, four_bit_alu_4_c_out,
       four_bit_alu_5_c_out, four_bit_alu_6_c_out, four_bit_alu_7_c_out;

  four_bit_ALU four_bit_alu_1 (
    .ALU_Ctrl(ALU_Ctrl), .A(A[3:0]), .B(B[3:0]), .C_in(ALU_Ctrl[2]), .R(Result[3:0]),
    .C_out(four_bit_alu_1_c_out));
  four_bit_ALU four_bit_alu_2 (
    .ALU_Ctrl(ALU_Ctrl), .A(A[7:4]), .B(B[7:4]), .C_in(four_bit_alu_1_c_out), .R(Result[7:4]),
    .C_out(four_bit_alu_2_c_out));
  four_bit_ALU four_bit_alu_3 (
    .ALU_Ctrl(ALU_Ctrl), .A(A[11:8]), .B(B[11:8]), .C_in(four_bit_alu_2_c_out), .R(Result[11:8]),
    .C_out(four_bit_alu_3_c_out));
  four_bit_ALU four_bit_alu_4 (
    .ALU_Ctrl(ALU_Ctrl), .A(A[15:12]), .B(B[15:12]), .C_in(four_bit_alu_3_c_out), .R(Result[15:12]),
    .C_out(four_bit_alu_4_c_out));
  four_bit_ALU four_bit_alu_5 (
    .ALU_Ctrl(ALU_Ctrl), .A(A[19:16]), .B(B[19:16]), .C_in(four_bit_alu_4_c_out), .R(Result[19:16]),
    .C_out(four_bit_alu_5_c_out));
  four_bit_ALU four_bit_alu_6 (
    .ALU_Ctrl(ALU_Ctrl), .A(A[23:20]), .B(B[23:20]), .C_in(four_bit_alu_5_c_out), .R(Result[23:20]),
    .C_out(four_bit_alu_6_c_out));
  four_bit_ALU four_bit_alu_7 (
    .ALU_Ctrl(ALU_Ctrl), .A(A[27:24]), .B(B[27:24]), .C_in(four_bit_alu_6_c_out), .R(Result[27:24]),
    .C_out(four_bit_alu_7_c_out));
  four_bit_ALU four_bit_alu_8 (
    .ALU_Ctrl(ALU_Ctrl), .A(A[31:28]), .B(B[31:28]), .C_in(four_bit_alu_7_c_out), .R(Result[31:28]),
    .C_out(C_out));
endmodule

module one_bit_adder (
  input  A,
  input  B,
  input  C_in,
  output S,
  output C_out
);

  wire and_1_out, and_2_out, xor_1_out;

  xor xor_1 (xor_1_out, A, B);
  xor xor_2 (S, xor_1_out, C_in);
  and and_1 (and_1_out, xor_1_out, C_in);
  and and_2 (and_2_out, A, B);
  or or_1 (C_out, and_1_out, and_2_out);
endmodule

module ALU_Control (
  input  I30,
  input  I14,
  input  I13,
  input  I12,
  input  I6,
  input  I5,
  input  I4,
  output ALU_Ctrl3,
  output ALU_Ctrl2,
  output ALU_Ctrl1,
  output ALU_Ctrl0,
  output ALU_Src
);

  wire and_2_out, and_3_out, and_4_out, and_5_out, and_6_out, and_7_out, not_1_out, not_2_out, not_3_out,
       not_4_out, not_5_out, not_6_out, not_7_out;

  not not_1 (not_1_out, I30);
  not not_2 (not_2_out, I14);
  not not_3 (not_3_out, I13);
  not not_4 (not_4_out, I12);
  not not_5 (not_5_out, I6);
  not not_6 (not_6_out, I5);
  not not_7 (not_7_out, I4);
  and and_1 (ALU_Ctrl2, I30, not_3_out, I5);
  or or_1 (ALU_Ctrl1, not_3_out, not_7_out);
  and and_2 (and_2_out, I13, not_4_out, not_6_out);
  and and_3 (and_3_out, not_1_out, I13, not_4_out, not_5_out, I4);
  and and_4 (and_4_out, not_2_out, I13, not_4_out);
  and and_5 (and_5_out, I13, not_4_out, not_7_out);
  and and_6 (and_6_out, I13, not_4_out, I6);
  and and_7 (and_7_out, I30, I13, not_4_out);
  or or_2 (ALU_Ctrl0, not_2_out, and_2_out, and_3_out);
  or or_3 (ALU_Src, not_6_out, and_4_out, and_5_out, and_6_out, and_7_out);

  assign ALU_Ctrl3 = 1'b0;
endmodule
